// Logisim project cpu.circ as structural Verilog: 1 circuit, main circuit cpu
module cpu (
  input  clk,
  input  [31:0] INSTRUCTION,
  input  [31:0] READ_DATA,
  output [31:0] WRITE_ADDRESS,
  output [31:0] PROGRAM_COUNTER,
  output [31:0] ra,
  output [31:0] sp,
  output [31:0] t0,
  output [31:0] t1,
  output [31:0] t2,
  output [31:0] s0,
  output [31:0] s1,
  output [31:0] a0,
  output [31:0] tohost,
  output [3:0] WRITE_ENABLE,
  output [31:0] WRITE_DATA
);

  wire [2:0] funct3;
  wire [4:0] imm;
  wire [6:0] funct7;
  wire [19:0] next_instruction;
  wire [31:0] adder_1_out, ALU_data, Immediate, multiplexer_1_out, RD1, RD2;

  Adder #(.width(32)) adder_1 (.a(PROGRAM_COUNTER), .b(32'h4), .out(adder_1_out));  // open: cin, cout
  Register #(.width(32)) PC (.D(adder_1_out), .clk(clk), .Q(PROGRAM_COUNTER));  // open: en, clr
  Register #(.width(32)) register_1 (
    .D(INSTRUCTION), .clk(clk), .Q({funct7, imm, next_instruction[19:15], funct3, next_instruction[11:0]}));  // open: en, clr
  control_logic control_logic_1 (.inst({funct7, imm, next_instruction[19:15], funct3, next_instruction[11:0]}));  // open: CSRWen, PCSel, RegWEn, ImmSel, BrUn, ASel, BSel, ALUSel, MemRW, WBSel, CSRSel, BrEq, BrLt
  imm_gen imm_gen_1 (
    .inst({funct7, imm, next_instruction[19:15], funct3, next_instruction[11:0]}), .ImmSel(3'b001),
    .imm(Immediate));
  regfile regfile_1 (
    .rs1(next_instruction[19:15]), .rs2(imm), .rd(next_instruction[11:7]), .Write_Data(ALU_data),
    .RegWEn(1'b1), .clk(clk), .ra(ra), .sp(sp), .t0(t0), .t1(t1), .t2(t2), .s0(s0), .s1(s1), .a0(a0),
    .Read_Data_1(RD1), .Read_Data_2(RD2));
  // branch_comp branch_comp_1: pin names not known
  Multiplexer #(.enable("false"), .width(32)) multiplexer_1 (
    .in0(RD2), .in1(Immediate), .out(multiplexer_1_out), .sel(1'b1));
  alu alu_1 (.Result(ALU_data), .A(RD1), .B(multiplexer_1_out), .ALUSel(4'b0000));
  csr csr_1 (.tohost(tohost));  // open: CSR_address, CSR_din, CSR_WE, clk

  // Other names for the same wires on the sheet: next_instruction (some bits) = {funct7, imm, funct3}; rs2[4:0] = imm;
  //   imm[11:5] = funct7; opcode[6:0] = next_instruction[6:0]; rd[4:0] = next_instruction[11:7];
  //   rs1[4:0] = next_instruction[19:15]

  // Notes on the sheet:
  //   Output to IMEM
  //   IMEM (do **NOT** move this)
  //   Inputs from IMEM
  //   It is OK to move the PC, RegFile, ALU, MEM, Branch Comp, Imm Gen, and Control Logic to wherever is most convenient for you when constructing your CPU, and to delete this text
  //   Inputs/Outputs for testing. Do **NOT** move these.
  //   Outputs To DMEM
  //   DMEM (do **NOT** move this)
  //   Inputs From DMEM
endmodule
